// Logisim project Circuito.circ as structural Verilog
module Memoria_de_dados (
  input  Mem_Write,
  input  Mem_Read,
  input  [31:0] EL,
  input  [31:0] WD,
  output [31:0] out_5
);

  wire clock_1_out;

  RAM #(.addrWidth(24), .dataWidth(32), .bus("separate")) ram_1 (
    .addr(EL[23:0]), .din(WD), .data(out_5), .str(Mem_Write), .clk(clock_1_out), .ld(Mem_Read));  // open: sel, clr
  Clock clock_1 (.out(clock_1_out));
endmodule

module \Memoria_de_Instruções  (
  input  [31:0] \Endereço ,
  output [31:0] \Instrução 
);

  ROM #(.addrWidth(24), .dataWidth(32)) rom_1 (.addr(\Endereço [25:2]), .data(\Instrução ));  // open: sel
endmodule

module Extensor_de_Sinal (
  input  [15:0] in_1,
  output [31:0] out_2
);


  assign out_2 = {{17{in_1[15]}}, in_1[14:0]};
endmodule

module decodificador (
  input  [31:0] instrucao,
  output [5:0] opcode,
  output [5:0] funct,
  output [4:0] shamt,
  output [4:0] rd,
  output [4:0] rt,
  output [4:0] rs,
  output [15:0] imm,
  output [25:0] addr
);

  wire I_out, J_out, Jal_out, or_1_out, R_out;
  wire [4:0] demultiplexer_1_out1, demultiplexer_1_out1_2, demultiplexer_2_out0;
  wire [25:0] \Não_R ;
  wire [25:21] demultiplexer_2_out0_2;

  and J (J_out, ~instrucao[31], ~instrucao[30], ~instrucao[29], ~instrucao[28], instrucao[27], ~instrucao[26]);  // AND_Gate
  Demultiplexer #(.width(26), .enable("false")) demultiplexer_1 (
    .out0(\Não_R ), .out1({demultiplexer_1_out1_2, demultiplexer_1_out1, rd, shamt, funct}),
    .in(instrucao[25:0]), .sel(R_out));
  and R (R_out, ~instrucao[31], ~instrucao[30], ~instrucao[29], ~instrucao[28], ~instrucao[27], ~instrucao[26]);  // AND_Gate
  and Jal (Jal_out, ~instrucao[31], ~instrucao[30], ~instrucao[29], ~instrucao[28], instrucao[27], instrucao[26]);  // AND_Gate
  or or_1 (or_1_out, J_out, Jal_out);
  Demultiplexer #(.width(26), .enable("false")) demultiplexer_2 (
    .out0({demultiplexer_2_out0_2, demultiplexer_2_out0, imm}), .out1(addr), .in(\Não_R ), .sel(or_1_out));
  and I (I_out, ~R_out, ~or_1_out);  // AND_Gate
  Multiplexer #(.width(5), .enable("false")) multiplexer_1 (
    .in0(demultiplexer_1_out1), .in1(demultiplexer_2_out0), .out(rt), .sel(I_out));
  Multiplexer #(.width(5), .enable("false")) multiplexer_2 (
    .in0(demultiplexer_1_out1_2), .in1(demultiplexer_2_out0_2), .out(rs), .sel(I_out));

  assign opcode = instrucao[31:26];
endmodule
