// Logisim project circuito.circ as structural Verilog
module \Unidade_de_Controle_para_Instrução_R  (
  input  [5:0] OpCode,
  output RegDst,
  output AluSrc,
  output MemToReg,
  output WriteReg,
  output [1:0] AluOp
);

  not not_1 (AluSrc, RegDst);
  and and_1 (RegDst, ~OpCode[0], ~OpCode[1], ~OpCode[2], ~OpCode[3], ~OpCode[4], ~OpCode[5]);  // AND_Gate

  assign AluOp = 2'b00;
  assign MemToReg = AluSrc;
  assign WriteReg = RegDst;
endmodule

module Unidade_de_Controle_da_ULA (
  input  [5:0] Funct,
  input  [1:0] AluOp,
  output [3:0] Op
);

  Multiplexer #(.select(2), .width(4)) multiplexer_1 (
    .in0(Funct[5:2]), .in1(4'b0000), .in2(4'b0000), .in3(4'b0000), .out(Op), .sel(AluOp));  // open: en
endmodule
